// Digital circuit Acumulador.dig as structural Verilog
module Acumulador (
  input  NLa,
  input  Ea,
  input  Clk,
  input  I0,
  input  I1,
  input  I2,
  input  I3,
  input  I4,
  input  I5,
  input  I6,
  input  I7,
  output S0,
  output S1,
  output S2,
  output S3,
  output S4,
  output S5,
  output S6,
  output S7
);

  wire not_1_out;

  not not_1 (not_1_out, NLa);
  Register register_1 (
    .Clk(Clk), .R(Ea), .D8(I0), .W(not_1_out), .Clr(1'b0), .D9(I1), .D10(I2), .D11(I3), .D12(I4), .D13(I5),
    .D14(I6), .D15(I7), .Q8(S0), .Q9(S1), .Q10(S2), .Q11(S3), .Q12(S4), .Q13(S5), .Q14(S6), .Q15(S7));
endmodule
