// Digital circuit Adder.dig as structural Verilog
module Adder (
  input  A0,
  input  B0,
  input  A1,
  input  B1,
  input  A2,
  input  B2,
  input  A3,
  input  B3,
  input  A4,
  input  B4,
  input  A5,
  input  B5,
  input  A6,
  input  B6,
  input  A7,
  input  B7,
  output S0,
  output S1,
  output S2,
  output S3,
  output S4,
  output S5,
  output S6,
  output S7,
  output out_25
);

  wire somador_2_cout, somador_3_cout, somador_4_cout, somador_5_cout, somador_6_cout, somador_7_cout,
       somador_8_cout;

  somador somador_1 (.A(A7), .B(B7), .Cin(somador_2_cout), .S(S7), .Cout(out_25));
  somador somador_2 (.A(A6), .B(B6), .Cin(somador_3_cout), .S(S6), .Cout(somador_2_cout));
  somador somador_3 (.A(A5), .B(B5), .Cin(somador_4_cout), .S(S5), .Cout(somador_3_cout));
  somador somador_4 (.A(A4), .B(B4), .Cin(somador_5_cout), .S(S4), .Cout(somador_4_cout));
  somador somador_5 (.A(A3), .B(B3), .Cin(somador_6_cout), .S(S3), .Cout(somador_5_cout));
  somador somador_6 (.A(A2), .B(B2), .Cin(somador_7_cout), .S(S2), .Cout(somador_6_cout));
  somador somador_7 (.A(A1), .B(B1), .Cin(somador_8_cout), .S(S1), .Cout(somador_7_cout));
  somador somador_8 (.A(A0), .B(B0), .Cin(1'b0), .S(S0), .Cout(somador_8_cout));
endmodule
