// Digital circuit CPU.dig as structural Verilog
module CPU (
  input  Op0,
  input  Op1,
  input  Op2
);

  wire Ad, alucpu_1_p1, alucpu_1_p2, alucpu_1_p3, alucpu_1_p4, alucpu_1_p5, alucpu_1_p6, alucpu_1_p7,
       alucpu_1_p8, alucpu_1_p9, alucpu_1_p10, alucpu_1_p11, alucpu_1_p16, alucpu_1_p17, alucpu_1_p18,
       alucpu_1_p19, alucpu_1_p20, alucpu_1_p21, alucpu_1_p22, alucpu_1_p23, alucpu_1_p24, alucpu_1_p25,
       alucpu_1_p26, alucpu_1_p27, alucpu_1_p28, alucpu_1_p29, alucpu_1_p30, alucpu_1_p31, Clk, Clr, Cp, Ea,
       Ep, instruction_register_1_c0, memory_address_register_1_s0, memory_address_register_1_s1,
       memory_address_register_1_s2, memory_address_register_1_s3, memory_address_register_1_s4,
       memory_address_register_1_s5, memory_address_register_1_s6, memory_address_register_1_s7, NCE, NEi,
       NLa, NLb, NLi, NLm, NLo, ring_counter_1_p2, ring_counter_1_p3, ring_counter_1_p4;
  wire [3:0] register_out_1_s3, register_out_1_s7;

  DiodeForward diodeforward_1 (.in(ring_counter_1_p4), .out(NLa));
  PullDown pulldown_1 (.out(NLa));
  PullDown pulldown_2 (.out(Ea));
  PullDown pulldown_3 (.out(Clk));
  DiodeForward diodeforward_2 (.in(ring_counter_1_p3), .out(NLa));
  DiodeForward diodeforward_3 (.in(ring_counter_1_p2), .out(NLa));
  DiodeForward diodeforward_4 (.in(ring_counter_1_p4), .out(NLb));
  PullDown pulldown_4 (.out(NLb));
  PullDown pulldown_5 (.out(Clk));
  DiodeForward diodeforward_5 (.in(ring_counter_1_p3), .out(NLb));
  DiodeForward diodeforward_6 (.in(ring_counter_1_p2), .out(NLb));
  PullDown pulldown_6 (.out(Clk));
  DiodeForward diodeforward_7 (.in(ring_counter_1_p4), .out(NLo));
  DiodeForward diodeforward_8 (.in(ring_counter_1_p3), .out(NLo));
  DiodeForward diodeforward_9 (.in(ring_counter_1_p2), .out(NLo));
  PullDown pulldown_7 (.out(NLo));
  LED led (.in(alucpu_1_p11));
  LED eq (.in(alucpu_1_p10));
  LED plus (.in(alucpu_1_p9));
  // ALUCPU alucpu_1: pin names not known; wires that end beside it: alucpu_1_p1, alucpu_1_p2, alucpu_1_p3, alucpu_1_p4, alucpu_1_p5, alucpu_1_p6, alucpu_1_p7, alucpu_1_p8, alucpu_1_p9, alucpu_1_p10, alucpu_1_p11, Ea, Op2, Op1, Op0, alucpu_1_p16, alucpu_1_p17, alucpu_1_p18, alucpu_1_p19, alucpu_1_p20, alucpu_1_p21, alucpu_1_p22, alucpu_1_p23, alucpu_1_p24, alucpu_1_p25, alucpu_1_p26, alucpu_1_p27, alucpu_1_p28, alucpu_1_p29, alucpu_1_p30, alucpu_1_p31
  Seven_Seg_Hex seven_seg_hex_1 (.d(register_out_1_s3), .dp(1'b0));
  Seven_Seg_Hex seven_seg_hex_2 (.d(register_out_1_s7), .dp(1'b0));
  Acumulador acumulador_1 (
    .NLa(NLa), .Ea(Ea), .Clk(Clk), .I0(alucpu_1_p8), .I1(alucpu_1_p7), .I2(alucpu_1_p6), .I3(alucpu_1_p5),
    .I4(alucpu_1_p4), .I5(alucpu_1_p3), .I6(alucpu_1_p2), .I7(alucpu_1_p1), .S0(alucpu_1_p31),
    .S1(alucpu_1_p29), .S2(alucpu_1_p27), .S3(alucpu_1_p25), .S4(alucpu_1_p23), .S5(alucpu_1_p21),
    .S6(alucpu_1_p19), .S7(alucpu_1_p17));
  Button u_Clr (.out(Clr));
  Button u_Clk (.out(Clk));
  Register_out register_out_1 (
    .NLo(NLo), .Clk(Clk), .I0(alucpu_1_p8), .I1(alucpu_1_p7), .I2(alucpu_1_p6), .I3(alucpu_1_p5),
    .I4(alucpu_1_p4), .I5(alucpu_1_p3), .I6(alucpu_1_p2), .I7(alucpu_1_p1), .S0(register_out_1_s3[0]),
    .S1(register_out_1_s3[1]), .S2(register_out_1_s3[2]), .S3(register_out_1_s3[3]),
    .S4(register_out_1_s7[0]), .S5(register_out_1_s7[1]), .S6(register_out_1_s7[2]), .S7(register_out_1_s7[3]));
  Register_B register_b_1 (
    .NLb(NLb), .Clk(Clk), .I0(alucpu_1_p8), .I1(alucpu_1_p7), .I2(alucpu_1_p6), .I3(alucpu_1_p5),
    .I4(alucpu_1_p4), .I5(alucpu_1_p3), .I6(alucpu_1_p2), .I7(alucpu_1_p1), .S0(alucpu_1_p30),
    .S1(alucpu_1_p28), .S2(alucpu_1_p26), .S3(alucpu_1_p24), .S4(alucpu_1_p22), .S5(alucpu_1_p20),
    .S6(alucpu_1_p18), .S7(alucpu_1_p16));
  Memory_Address_Register memory_address_register_1 (
    .NLm(NLm), .Clk(Clk), .I0(alucpu_1_p8), .I1(alucpu_1_p7), .I2(alucpu_1_p6), .I3(alucpu_1_p5),
    .I4(alucpu_1_p4), .I5(alucpu_1_p3), .I6(alucpu_1_p2), .I7(alucpu_1_p1),
    .S0(memory_address_register_1_s0), .S1(memory_address_register_1_s1), .S2(memory_address_register_1_s2),
    .S3(memory_address_register_1_s3), .S4(memory_address_register_1_s4), .S5(memory_address_register_1_s5),
    .S6(memory_address_register_1_s6), .S7(memory_address_register_1_s7));
  Program_Counter program_counter_1 (
    .Cp(Cp), .Ep(Ep), .NClr(Clr), .NClk(Clk), .S0(alucpu_1_p8), .S1(alucpu_1_p7), .S2(alucpu_1_p6),
    .S3(alucpu_1_p5));  // open: S4, S5, S6, S7
  Instruction_Register instruction_register_1 (
    .NEi(NEi), .Clr(Clr), .Clk(Clk), .NLi(NLi), .I0(alucpu_1_p8), .I1(alucpu_1_p7), .I2(alucpu_1_p6),
    .I3(alucpu_1_p5), .I4(alucpu_1_p4), .I5(alucpu_1_p3), .I6(alucpu_1_p2), .I7(alucpu_1_p1),
    .C0(instruction_register_1_c0), .C1(instruction_register_1_c0), .C2(instruction_register_1_c0),
    .C3(instruction_register_1_c0), .Op0(alucpu_1_p4), .Op1(alucpu_1_p3), .Op2(alucpu_1_p2), .Op3(alucpu_1_p1));
  Random_Access_Memory random_access_memory_1 (
    .I0(memory_address_register_1_s0), .I1(memory_address_register_1_s1), .I2(memory_address_register_1_s2),
    .I3(memory_address_register_1_s3), .I4(memory_address_register_1_s4), .I5(memory_address_register_1_s5),
    .I6(memory_address_register_1_s6), .I7(memory_address_register_1_s7), .NCe(NCE), .Clr(Clr), .Clk(Clk),
    .A(memory_address_register_1_s0), .B(memory_address_register_1_s1), .C(memory_address_register_1_s2),
    .D(Ad), .S0(alucpu_1_p8), .S1(alucpu_1_p7), .S2(alucpu_1_p6), .S3(alucpu_1_p5), .S4(alucpu_1_p4),
    .S5(alucpu_1_p3), .S6(alucpu_1_p2), .S7(alucpu_1_p1));
  DiodeForward diodeforward_10 (.in(ring_counter_1_p3), .out(NEi));
  DiodeForward diodeforward_11 (.in(ring_counter_1_p2), .out(NEi));
  DiodeForward diodeforward_12 (.in(ring_counter_1_p4), .out(NLi));
  DiodeForward diodeforward_13 (.in(ring_counter_1_p4), .out(NEi));
  DiodeForward diodeforward_14 (.in(ring_counter_1_p3), .out(NLi));
  PullDown pulldown_8 (.out(NLi));
  PullDown pulldown_9 (.out(Clk));
  PullDown pulldown_10 (.out(Clr));
  PullDown pulldown_11 (.out(NEi));
  DiodeForward diodeforward_15 (.in(ring_counter_1_p4), .out(NCE));
  DiodeForward diodeforward_16 (.in(ring_counter_1_p4), .out(Ad));
  DiodeForward diodeforward_17 (.in(ring_counter_1_p3), .out(NCE));
  DiodeForward diodeforward_18 (.in(ring_counter_1_p3), .out(Ad));
  PullDown pulldown_12 (.out(NCE));
  PullDown pulldown_13 (.out(Clr));
  PullDown pulldown_14 (.out(Clk));
  PullDown pulldown_15 (.out(Ad));
  DiodeForward diodeforward_19 (.in(ring_counter_1_p2), .out(NLm));
  DiodeForward diodeforward_20 (.in(ring_counter_1_p3), .out(NLm));
  PullDown pulldown_16 (.out(Clk));
  PullDown pulldown_17 (.out(NLm));
  DiodeForward diodeforward_21 (.in(ring_counter_1_p3), .out(Cp));
  DiodeForward diodeforward_22 (.in(ring_counter_1_p4), .out(Ep));
  // Ring_Counter ring_counter_1: pin names not known; wires that end beside it: Ea, ring_counter_1_p2, ring_counter_1_p3, ring_counter_1_p4, Clr, Clk
  PullDown pulldown_18 (.out(Ep));
  PullDown pulldown_19 (.out(Clr));
  PullDown pulldown_20 (.out(Clk));
  PullDown pulldown_21 (.out(Cp));
  // also tied to GND on the sheet: instruction_register_1_c0

  // Other names for the same wires on the sheet: Eu = Ea

  // Notes on the sheet:
  //   FETCH:
  //   T2:
  //   Cp Ep NLm NCE Ad  NLi NEi NLa Ea  Eu NLb NLa
  //   1    0     1     1    1     1   1     1    0   0    1     1
  //   T1:
  //   Cp Ep NLm NCE Ad  NLi NEi NLa Ea  Eu NLb NLa
  //   1    0     1     1    1     1   1     1    0   0    1     1
  //   T0:
  //   Cp Ep NLm NCE Ad  NLi NEi NLa Ea  Eu NLb NLa
  //   0    1     0     1    1     1   1     1    0   0    1     1
endmodule
