// Digital circuit Controller.dig as structural Verilog
module Controller (
  input  Clk,
  input  Clr,
  input  I0,
  input  I1,
  input  I2,
  input  I3,
  output Ep,
  output Cp,
  output NLm,
  output NEi,
  output NCE,
  output NLi,
  output Ea,
  output NLa,
  output Op0,
  output Op1,
  output Op2,
  output Eu,
  output NLb,
  output NLo,
  output HLT
);

  wire and_2_out, and_3_out, and_4_out, and_5_out, and_6_out, and_7_out, and_8_out, and_9_out, and_10_out,
       and_12_out, and_15_out, and_16_out, and_17_out, and_18_out, and_19_out, and_20_out, and_21_out,
       and_22_out, and_23_out, and_24_out, and_25_out, and_26_out, and_27_out, or_3_out, or_6_out, or_9_out,
       ring_counter_1_p5, ring_counter_1_p6, ring_counter_1_p7, seletor_1_s0, seletor_1_s1, seletor_1_s2,
       seletor_1_s3, seletor_1_s4, seletor_1_s5, seletor_1_s6, seletor_1_s7;

  // Ring_Counter ring_counter_1: pin names not known; wires that end beside it: Clk, Clr, Ep, Cp, ring_counter_1_p5, ring_counter_1_p6, ring_counter_1_p7
  Seletor seletor_1 (
    .A(I0), .B(I1), .C(I2), .D(I3), .S0(seletor_1_s0), .S1(seletor_1_s1), .S2(seletor_1_s2),
    .S3(seletor_1_s3), .S4(seletor_1_s4), .S5(seletor_1_s5), .S6(seletor_1_s6), .S7(seletor_1_s7), .S8(HLT));
  or or_1 (NLm, ring_counter_1_p5, Cp);
  or or_2 (NCE, Cp, Ep);
  or or_3 (or_3_out, ring_counter_1_p6, Cp, Ep);
  and and_1 (NLi, seletor_1_s0, or_3_out);
  or or_4 (NEi, ring_counter_1_p5, Cp, Ep);
  or or_5 (NLa, ring_counter_1_p5, Cp, Ep);
  or or_6 (or_6_out, ring_counter_1_p7, ring_counter_1_p6);
  and and_2 (and_2_out, seletor_1_s0, or_6_out);
  and and_3 (and_3_out, seletor_1_s1, or_6_out);
  and and_4 (and_4_out, seletor_1_s2, or_6_out);
  and and_5 (and_5_out, seletor_1_s3, or_6_out);
  and and_6 (and_6_out, seletor_1_s4, or_6_out);
  or or_7 (Ea, and_9_out, and_8_out, and_7_out, and_6_out, and_5_out, and_4_out, and_3_out, and_2_out);
  and and_7 (and_7_out, seletor_1_s5, or_6_out);
  and and_8 (and_8_out, seletor_1_s6, or_6_out);
  and and_9 (and_9_out, seletor_1_s7, ring_counter_1_p6);
  and and_10 (and_10_out, seletor_1_s6, seletor_1_s2);
  DiodeForward diodeforward_1 (.in(and_10_out), .out(Op2));
  DiodeForward diodeforward_2 (.in(and_10_out), .out(Op0));
  and and_11 (Op2, seletor_1_s5, seletor_1_s2);
  and and_12 (and_12_out, seletor_1_s4, seletor_1_s2);
  DiodeForward diodeforward_3 (.in(and_12_out), .out(Op1));
  DiodeForward diodeforward_4 (.in(and_12_out), .out(Op0));
  PullDown pulldown_1 (.out(Op2));
  and and_13 (Op1, seletor_1_s3, seletor_1_s2);
  PullDown pulldown_2 (.out(Op1));
  and and_14 (Op0, seletor_1_s2, ring_counter_1_p7);
  PullDown pulldown_3 (.out(Op0));
  and and_15 (and_15_out, seletor_1_s1, ring_counter_1_p7);
  and and_16 (and_16_out, seletor_1_s2, ring_counter_1_p7);
  and and_17 (and_17_out, seletor_1_s3, ring_counter_1_p7);
  and and_18 (and_18_out, seletor_1_s4, ring_counter_1_p7);
  or or_8 (Eu, and_20_out, and_19_out, and_18_out, and_17_out, and_16_out, and_15_out);
  and and_19 (and_19_out, seletor_1_s5, ring_counter_1_p7);
  and and_20 (and_20_out, seletor_1_s6, ring_counter_1_p7);
  or or_9 (or_9_out, ring_counter_1_p6, ring_counter_1_p5, Cp, Ep);
  and and_21 (and_21_out, seletor_1_s1, or_9_out);
  and and_22 (and_22_out, seletor_1_s2, or_9_out);
  and and_23 (and_23_out, seletor_1_s3, or_9_out);
  and and_24 (and_24_out, seletor_1_s4, or_9_out);
  and and_25 (and_25_out, seletor_1_s5, or_9_out);
  or or_10 (NLb, and_27_out, and_26_out, and_25_out, and_24_out, and_23_out, and_22_out, and_21_out);
  and and_26 (and_26_out, seletor_1_s6, or_9_out);
  and and_27 (and_27_out, seletor_1_s7, ring_counter_1_p6);
  or or_11 (NLo, ring_counter_1_p5, Cp, Ep);

  // Notes on the sheet:
  //   EXECUTE:
  //   Cp Ep NLm NCE NLi NEi NLa Ea  Eu NLb NLa
  //   0    1     0     1     1   1     1    0   0    1     1
  //   FETCH:
  //   T2:
  //   Cp Ep NLm NCE NLi NEi NLa Ea  Eu NLb NLa
  //   1    0     1     1    1   1     1    0   0    1     1
  //   T1:
  //   Cp Ep NLm NCE NLi NEi NLa Ea  Eu NLb NLa
  //   1    0     1     1     1   1     1    0   0    1     1
  //   T0:
  //   Cp Ep NLm NCE  NLi NEi NLa Ea  Eu NLb NLa
  //   0    1     0     1      1   1     1    0   0    1     1
  //   000 - Sum
  //   001 - Sub
  //   010 - Comp
  //   011 - Multi
  //   100 - ShiftR
  //   101 - ShiftL
endmodule
