// Digital circuit Instruction Register.dig as structural Verilog
module Instruction_Register (
  input  NEi,
  input  Clr,
  input  Clk,
  input  NLi,
  input  I0,
  input  I1,
  input  I2,
  input  I3,
  input  I4,
  input  I5,
  input  I6,
  input  I7,
  output C0,
  output C1,
  output C2,
  output C3,
  output Op0,
  output Op1,
  output Op2,
  output Op3
);

  wire not_1_out, not_2_out;

  Register register_1 (
    .Clk(Clk), .R(not_1_out), .D8(I0), .W(not_2_out), .Clr(Clr), .D9(I1), .D10(I2), .D11(I3), .D12(I4),
    .D13(I5), .D14(I6), .D15(I7), .Q8(C0), .Q9(C1), .Q10(C2), .Q11(C3), .Q12(Op0), .Q13(Op1), .Q14(Op2),
    .Q15(Op3));
  not not_1 (not_1_out, NEi);
  not not_2 (not_2_out, NLi);
endmodule
