// Digital circuit Memory Address Register.dig as structural Verilog
module Memory_Address_Register (
  input  NLm,
  input  Clk,
  input  I0,
  input  I1,
  input  I2,
  input  I3,
  output S0,
  output S1,
  output S2,
  output S3
);

  wire not_1_out, register_1_q12;

  not not_1 (not_1_out, NLm);
  Register register_1 (
    .Clk(Clk), .R(1'b1), .D8(I0), .W(not_1_out), .Clr(1'b0), .D9(I1), .D10(I2), .D11(I3), .D12(1'b0),
    .D13(1'b0), .D14(1'b0), .D15(1'b0), .Q8(S0), .Q9(S1), .Q10(S2), .Q11(S3), .Q12(register_1_q12),
    .Q13(register_1_q12), .Q14(register_1_q12), .Q15(register_1_q12));
  // also tied to GND on the sheet: register_1_q12
endmodule
