// Digital circuit Register.dig as structural Verilog
module Register (
  input  Clk,
  input  R,
  input  D8,
  input  W,
  input  Clr,
  input  D9,
  input  D10,
  input  D11,
  input  D12,
  input  D13,
  input  D14,
  input  D15,
  output Q8,
  output Q9,
  output Q10,
  output Q11,
  output Q12,
  output Q13,
  output Q14,
  output Q15
);

  wire and_1_out, and_2_out, and_3_out, and_4_out, and_5_out, and_6_out, and_7_out, and_8_out, and_9_out,
       d_ff_1_q, d_ff_2_q, d_ff_3_q, d_ff_4_q, d_ff_5_q, d_ff_6_q, d_ff_7_q, d_ff_8_q, diodeforward_1_out,
       diodeforward_2_out, diodeforward_3_out, diodeforward_4_out, diodeforward_5_out, diodeforward_6_out,
       diodeforward_7_out, diodeforward_8_out;

  and and_1 (and_1_out, W, ~Clr);  // And
  and and_2 (and_2_out, D15, and_1_out);
  D_FF d_ff_1 (.D(and_2_out), .C(Clk), .Q(d_ff_1_q));  // open: nQ
  DiodeForward diodeforward_1 (.in(d_ff_1_q), .out(diodeforward_1_out));
  assign Q15 = R ? diodeforward_1_out : 1'bz;  // Driver driver_1
  PullDown pulldown_1 (.out(diodeforward_1_out));
  and and_3 (and_3_out, D14, and_1_out);
  D_FF d_ff_2 (.D(and_3_out), .C(Clk), .Q(d_ff_2_q));  // open: nQ
  DiodeForward diodeforward_2 (.in(d_ff_2_q), .out(diodeforward_2_out));
  assign Q14 = R ? diodeforward_2_out : 1'bz;  // Driver driver_2
  PullDown pulldown_2 (.out(diodeforward_2_out));
  and and_4 (and_4_out, D13, and_1_out);
  D_FF d_ff_3 (.D(and_4_out), .C(Clk), .Q(d_ff_3_q));  // open: nQ
  DiodeForward diodeforward_3 (.in(d_ff_3_q), .out(diodeforward_3_out));
  assign Q13 = R ? diodeforward_3_out : 1'bz;  // Driver driver_3
  PullDown pulldown_3 (.out(diodeforward_3_out));
  and and_5 (and_5_out, D12, and_1_out);
  D_FF d_ff_4 (.D(and_5_out), .C(Clk), .Q(d_ff_4_q));  // open: nQ
  DiodeForward diodeforward_4 (.in(d_ff_4_q), .out(diodeforward_4_out));
  assign Q12 = R ? diodeforward_4_out : 1'bz;  // Driver driver_4
  PullDown pulldown_4 (.out(diodeforward_4_out));
  and and_6 (and_6_out, D11, and_1_out);
  D_FF d_ff_5 (.D(and_6_out), .C(Clk), .Q(d_ff_5_q));  // open: nQ
  DiodeForward diodeforward_5 (.in(d_ff_5_q), .out(diodeforward_5_out));
  assign Q11 = R ? diodeforward_5_out : 1'bz;  // Driver driver_5
  PullDown pulldown_5 (.out(diodeforward_5_out));
  and and_7 (and_7_out, D10, and_1_out);
  D_FF d_ff_6 (.D(and_7_out), .C(Clk), .Q(d_ff_6_q));  // open: nQ
  DiodeForward diodeforward_6 (.in(d_ff_6_q), .out(diodeforward_6_out));
  assign Q10 = R ? diodeforward_6_out : 1'bz;  // Driver driver_6
  PullDown pulldown_6 (.out(diodeforward_6_out));
  and and_8 (and_8_out, D9, and_1_out);
  D_FF d_ff_7 (.D(and_8_out), .C(Clk), .Q(d_ff_7_q));  // open: nQ
  DiodeForward diodeforward_7 (.in(d_ff_7_q), .out(diodeforward_7_out));
  assign Q9 = R ? diodeforward_7_out : 1'bz;  // Driver driver_7
  PullDown pulldown_7 (.out(diodeforward_7_out));
  and and_9 (and_9_out, D8, and_1_out);
  D_FF d_ff_8 (.D(and_9_out), .C(Clk), .Q(d_ff_8_q));  // open: nQ
  DiodeForward diodeforward_8 (.in(d_ff_8_q), .out(diodeforward_8_out));
  assign Q8 = R ? diodeforward_8_out : 1'bz;  // Driver driver_8
  PullDown pulldown_8 (.out(diodeforward_8_out));
endmodule
