// Digital circuit Ring-Counter.dig as structural Verilog
module Ring_Counter (
  input  Clk,
  input  Clr,
  output Q0,
  output Q1,
  output Q2,
  output Q3,
  output Q4,
  output Q5
);

  wire d_ff_as_1_q, d_ff_as_2_q, d_ff_as_3_q, d_ff_as_4_q, d_ff_as_5_q, d_ff_as_6_q, d_ff_as_7_q;

  D_FF_AS d_ff_as_1 (.Set(Clr), .D(d_ff_as_7_q), .C(Clk), .Clr(1'b0), .Q(d_ff_as_1_q));  // open: nQ
  DiodeForward diodeforward_1 (.in(d_ff_as_1_q), .out(Q0));
  PullDown pulldown_1 (.out(Q0));
  D_FF_AS d_ff_as_2 (.Set(1'b0), .D(d_ff_as_1_q), .C(Clk), .Clr(Clr), .Q(d_ff_as_2_q));  // open: nQ
  DiodeForward diodeforward_2 (.in(d_ff_as_2_q), .out(Q1));
  PullDown pulldown_2 (.out(Q1));
  D_FF_AS d_ff_as_3 (.Set(1'b0), .D(d_ff_as_2_q), .C(Clk), .Clr(Clr), .Q(d_ff_as_3_q));  // open: nQ
  DiodeForward diodeforward_3 (.in(d_ff_as_3_q), .out(Q2));
  PullDown pulldown_3 (.out(Q2));
  D_FF_AS d_ff_as_4 (.Set(1'b0), .D(d_ff_as_3_q), .C(Clk), .Clr(Clr), .Q(d_ff_as_4_q));  // open: nQ
  DiodeForward diodeforward_4 (.in(d_ff_as_4_q), .out(Q3));
  PullDown pulldown_4 (.out(Q3));
  D_FF_AS d_ff_as_5 (.Set(1'b0), .D(d_ff_as_4_q), .C(Clk), .Clr(Clr), .Q(d_ff_as_5_q));  // open: nQ
  DiodeForward diodeforward_5 (.in(d_ff_as_5_q), .out(Q4));
  PullDown pulldown_5 (.out(Q4));
  D_FF_AS d_ff_as_6 (.Set(1'b0), .D(d_ff_as_5_q), .C(Clk), .Clr(Clr), .Q(d_ff_as_6_q));  // open: nQ
  DiodeForward diodeforward_6 (.in(d_ff_as_6_q), .out(Q5));
  PullDown pulldown_6 (.out(Q5));
  D_FF_AS d_ff_as_7 (.Set(1'b0), .D(d_ff_as_6_q), .C(Clk), .Clr(Clr), .Q(d_ff_as_7_q));  // open: nQ
endmodule
