// Digital circuit Seletor.dig as structural Verilog
module Seletor (
  input  A,
  input  B,
  input  C,
  input  D,
  output S0,
  output S1,
  output S2,
  output S3,
  output S4,
  output S5,
  output S6,
  output S7,
  output S8
);

  wire not_1_out, not_2_out, not_3_out, not_4_out;

  not not_1 (not_1_out, A);
  not not_2 (not_2_out, B);
  not not_3 (not_3_out, C);
  not not_4 (not_4_out, D);
  and and_1 (S0, not_4_out, not_3_out, not_2_out, not_1_out);
  and and_2 (S1, not_4_out, not_3_out, not_2_out, A);
  and and_3 (S2, not_4_out, not_3_out, B, not_1_out);
  and and_4 (S3, not_4_out, not_3_out, B, A);
  and and_5 (S4, not_4_out, not_2_out, not_1_out, C);
  and and_6 (S5, not_4_out, C, not_2_out, A);
  and and_7 (S6, not_4_out, C, B, not_1_out);
  and and_8 (S7, not_4_out, C, B, A);
  and and_9 (S8, D, not_3_out, not_2_out, not_1_out);

  // Notes on the sheet:
  //   0000
  //   0001
  //   0010
  //   0011
  //   0100
  //   0101
  //   0110
  //   0111
  //   1000
endmodule
