// Digital circuit Subtractor8.dig as structural Verilog
module Subtractor8 (
  input  A0,
  input  B0,
  input  A1,
  input  B1,
  input  A2,
  input  B2,
  input  A3,
  input  B3,
  input  A4,
  input  B4,
  input  A5,
  input  B5,
  input  A6,
  input  B6,
  input  A7,
  input  B7,
  output D0,
  output D1,
  output D2,
  output D3,
  output D4,
  output D5,
  output D6,
  output D7,
  output Neg
);

  wire subtrator_2_bt, subtrator_3_bt, subtrator_4_bt, subtrator_5_bt, subtrator_6_bt, subtrator_7_bt,
       subtrator_8_bt;

  Subtrator subtrator_1 (.B(B0), .A(A0), .BN(subtrator_2_bt), .Diff(D0), .BT(Neg));
  Subtrator subtrator_2 (.B(B1), .A(A1), .BN(subtrator_3_bt), .Diff(D1), .BT(subtrator_2_bt));
  Subtrator subtrator_3 (.B(B2), .A(A2), .BN(subtrator_4_bt), .Diff(D2), .BT(subtrator_3_bt));
  Subtrator subtrator_4 (.B(B3), .A(A3), .BN(subtrator_5_bt), .Diff(D3), .BT(subtrator_4_bt));
  Subtrator subtrator_5 (.B(B4), .A(A4), .BN(subtrator_6_bt), .Diff(D4), .BT(subtrator_5_bt));
  Subtrator subtrator_6 (.B(B5), .A(A5), .BN(subtrator_7_bt), .Diff(D5), .BT(subtrator_6_bt));
  Subtrator subtrator_7 (.B(B6), .A(A6), .BN(subtrator_8_bt), .Diff(D6), .BT(subtrator_7_bt));
  Subtrator subtrator_8 (.B(B7), .A(A7), .BN(1'b0), .Diff(D7), .BT(subtrator_8_bt));
endmodule
