// Digital circuit Subtrator.dig as structural Verilog
module Subtrator (
  input  B,
  input  A,
  input  BN,
  output Diff,
  output BT
);

  wire and_1_out, and_2_out, and_3_out, not_1_out, not_2_out, xor_1_out;

  xor xor_1 (xor_1_out, B, A);
  and and_1 (and_1_out, B, BN);
  and and_2 (and_2_out, B, not_1_out);
  not not_1 (not_1_out, A);
  and and_3 (and_3_out, BN, not_2_out);
  not not_2 (not_2_out, A);
  xor xor_2 (Diff, xor_1_out, BN);
  or or_1 (BT, and_1_out, and_2_out, and_3_out);
endmodule
