// Digital circuit comparador8bit.dig as structural Verilog
module comparador8bit (
  input  [7:0] A,
  input  [7:0] B,
  output A_lt_B,
  output A_eq_B,
  output A_gt_B
);

  wire comparador1bit_2_o_eq, comparador1bit_2_o_gt, comparador1bit_2_o_lt, comparador1bit_3_o_eq,
       comparador1bit_3_o_gt, comparador1bit_3_o_lt, comparador1bit_4_o_eq, comparador1bit_4_o_gt,
       comparador1bit_4_o_lt, comparador1bit_5_o_eq, comparador1bit_5_o_gt, comparador1bit_5_o_lt,
       comparador1bit_6_o_eq, comparador1bit_6_o_gt, comparador1bit_6_o_lt, comparador1bit_7_o_eq,
       comparador1bit_7_o_gt, comparador1bit_7_o_lt, meiocomparador_1_eq, meiocomparador_1_o_gt,
       meiocomparador_1_o_lt;

  comparador1bit comparador1bit_1 (
    .A(A[7]), .B(B[7]), .I__lt(comparador1bit_2_o_lt), .I__eq(comparador1bit_2_o_eq),
    .I__gt(comparador1bit_2_o_gt), .O_lt(A_lt_B), .O_eq(A_eq_B), .O_gt(A_gt_B));
  comparador1bit comparador1bit_2 (
    .A(A[6]), .B(B[6]), .I__lt(comparador1bit_3_o_lt), .I__eq(comparador1bit_3_o_eq),
    .I__gt(comparador1bit_3_o_gt), .O_lt(comparador1bit_2_o_lt), .O_eq(comparador1bit_2_o_eq),
    .O_gt(comparador1bit_2_o_gt));
  comparador1bit comparador1bit_3 (
    .A(A[5]), .B(B[5]), .I__lt(comparador1bit_4_o_lt), .I__eq(comparador1bit_4_o_eq),
    .I__gt(comparador1bit_4_o_gt), .O_lt(comparador1bit_3_o_lt), .O_eq(comparador1bit_3_o_eq),
    .O_gt(comparador1bit_3_o_gt));
  comparador1bit comparador1bit_4 (
    .A(A[4]), .B(B[4]), .I__lt(comparador1bit_5_o_lt), .I__eq(comparador1bit_5_o_eq),
    .I__gt(comparador1bit_5_o_gt), .O_lt(comparador1bit_4_o_lt), .O_eq(comparador1bit_4_o_eq),
    .O_gt(comparador1bit_4_o_gt));
  comparador1bit comparador1bit_5 (
    .A(A[3]), .B(B[3]), .I__lt(comparador1bit_6_o_lt), .I__eq(comparador1bit_6_o_eq),
    .I__gt(comparador1bit_6_o_gt), .O_lt(comparador1bit_5_o_lt), .O_eq(comparador1bit_5_o_eq),
    .O_gt(comparador1bit_5_o_gt));
  comparador1bit comparador1bit_6 (
    .A(A[2]), .B(B[2]), .I__lt(comparador1bit_7_o_lt), .I__eq(comparador1bit_7_o_eq),
    .I__gt(comparador1bit_7_o_gt), .O_lt(comparador1bit_6_o_lt), .O_eq(comparador1bit_6_o_eq),
    .O_gt(comparador1bit_6_o_gt));
  comparador1bit comparador1bit_7 (
    .A(A[1]), .B(B[1]), .I__lt(meiocomparador_1_o_lt), .I__eq(meiocomparador_1_eq),
    .I__gt(meiocomparador_1_o_gt), .O_lt(comparador1bit_7_o_lt), .O_eq(comparador1bit_7_o_eq),
    .O_gt(comparador1bit_7_o_gt));
  meiocomparador meiocomparador_1 (
    .A(A[0]), .B(B[0]), .O_lt(meiocomparador_1_o_lt), .eq(meiocomparador_1_eq), .O_gt(meiocomparador_1_o_gt));
endmodule
