// Digital circuit meiocomparador.dig as structural Verilog
module meiocomparador (
  input  A,
  input  B,
  output O_lt,
  output eq,
  output O_gt
);

  wire not_1_out, not_2_out;

  not not_1 (not_1_out, A);
  not not_2 (not_2_out, B);
  and and_1 (O_lt, not_1_out, B);
  xnor xnor_1 (eq, A, B);
  and and_2 (O_gt, A, not_2_out);
endmodule
