// Digital circuit somador.dig as structural Verilog
module somador (
  input  A,
  input  B,
  input  Cin,
  output S,
  output Cout
);

  wire and_1_out, and_2_out, and_3_out, and_4_out, xor_1_out;

  xor xor_1 (xor_1_out, A, B, Cin);
  and and_1 (and_1_out, A, B, Cin);
  and and_2 (and_2_out, A, B);
  and and_3 (and_3_out, A, Cin);
  and and_4 (and_4_out, Cin, B);
  or or_1 (S, xor_1_out, and_1_out);
  or or_2 (Cout, and_2_out, and_3_out, and_4_out);
endmodule
